# Fritzing sketch pi-temp-layout (saved by Fritzing 0.9.4)
circuit board: 8.46667cm x 5.64444cm
breadboards: 1

parts:
  MCU1 = Raspberry Pi Zero
  DS1 = DS18B20 1-Wire Temperature Sensor [part_number=DS18B20]
  R1 = Resistor [tolerance=±5% resistance=4.7k package="2010 [SMD]"]

nets:
  N1: MCU1.pin_1, DS1.VDD, R1.Pin_0
  N2: MCU1.pin_6, MCU1.pin_9, DS1.GND
  N3: MCU1.pin_11, DS1.DQ, R1.Pin_1

notes:
  v2021.03.08
